# Fritzing sketch Safety Printer (saved by Fritzing 0.9.6b)
perfboards: 1

parts:
  MCU = Arduino Nano (Rev3.0)
  R4 = Resistor [tolerance=±5% power=0.25 resistance=470 package=THT]
  R5 = Resistor [tolerance=±5% power=0.25 resistance=1000 package=THT]
  Flame_2 = JST-03JQ-BT [part_number=C3 package=THT]
  LED2 = LEDs [package=led10mm]
  S2 = Pushbutton [package="[SMD]"]
  R3 = Resistor [tolerance=±5% power=0.25 resistance=470 package=THT]
  Flame_1 = JST-03JQ-BT [part_number=C2 package=THT]
  Interlock_Relay = JST-03JQ-BT [part_number=C5 package=THT]
  R2 = Resistor [tolerance=±5% power=0.25 resistance=1000 package=THT]
  LED1 = LEDs [package=led10mm]
  R1 = Resistor [tolerance=±5% power=0.25 resistance=1000 package=THT]
  Smoke_Power = Header 2 [part_number=C1 package=jst-2-smd]
  Smoke_Signal = Header 2 [package=jst-2-smd]
  Emergency_Button = Screw terminal - 2 pins [part_number=C4 package=THT]
  Step_Up_Buck_Converter = RioRand LM2596
  Hot_end_temperature_NTC_Thermistor = Header 2 [part_number=C6 package=jst-2-pth-kit]
  R6 = Resistor [tolerance=±5% power=0.25 resistance=4.7k package=THT]

nets:
  N1: MCU.GND, R4.Pin_1, R5.Pin_1, Flame_2.pin2, R3.Pin_1, Flame_1.pin2, Interlock_Relay.pin2, R2.Pin_1, R1.Pin_1, Hot_end_temperature_NTC_Thermistor.1
  N2: MCU.D2, R6.Pin_0
  N3: MCU.D5, R2.Pin_0, Emergency_Button.pin2
  N4: MCU.D6, Interlock_Relay.pin3
  N5: MCU.D7, R1.Pin_0, Smoke_Signal.2
  N6: MCU.D8, Flame_2.pin1
  N7: MCU.D9, Flame_1.pin1
  N8: MCU.D10, LED2.A
  N9: MCU.D11/MOSI, S2.Pin_3
  N10: MCU.D12/MISO, LED1.A
  N11: MCU.5V, Flame_2.pin3, Flame_1.pin3, Interlock_Relay.pin1, Smoke_Signal.1, Emergency_Button.pin1, Step_Up_Buck_Converter.Pin_1
  N12: MCU.A7, Hot_end_temperature_NTC_Thermistor.2, R6.Pin_1
  N13: R4.Pin_0, LED1.C
  N14: R5.Pin_0, S2.Pin_1, S2.Pin_2
  N15: LED2.C, R3.Pin_0
  N16: Smoke_Power.2, Step_Up_Buck_Converter.Pin_4
  N17: Smoke_Power.1, Step_Up_Buck_Converter.Pin_3
